# Fritzing sketch ScrewShield (saved by Fritzing 0.9.6b)
circuit board: 9.65756cm x 8.92862cm
breadboards: 1

parts:
  Componente1 = Arduino Uno (Rev3)
  J5 = male pin header, 8 pins [form="♂ (male)"]
  J6 = female pin header, 10 pins [form="♀ (female)"]
  R1 = Resistor [tolerance=±5% power=0.25 resistance=10k package=THT]
  RESET = Momentary Switch [package=tactile-pth]
  POWER = LED - 5mm [color="Red (633nm)" current=0.030 package="5 mm [THT]"]
  R2 = Resistor [tolerance=±5% power=0.25 resistance=1k package=THT]
  C1 = Capacitor [package=cap-pth-5mm]
  C2 = Capacitor [package=cap-pth-5mm]
  J1 = screw terminal, 8 pins
  J2 = screw terminal, 10 pins
  J9 = screw terminal, 5 pins
  J11 = screw terminal, 5 pins
  J3 = screw terminal, 6 pins
  J4 = screw terminal, 7 pins
  J12 = male pin header, 8 pins [form="♂ (male)"]
  J13 = female pin header, 6 pins [form="♀ (female)"]

nets:
  N1: Componente1.A0, J3.pin1, J13.pin1
  N2: Componente1.A1, J3.pin2, J13.pin2
  N3: Componente1.A2, J3.pin3, J13.pin3
  N4: Componente1.A3, J3.pin4, J13.pin4
  N5: Componente1.A4/SDA, J6.pin2, J2.pin9, J3.pin5, J13.pin5
  N6: Componente1.A5/SCL, J6.pin1, J2.pin10, J3.pin6, J13.pin6
  N7: Componente1.D8, J6.pin10, J2.pin1
  N8: Componente1.D9_PWM, J6.pin9, J2.pin2
  N9: Componente1.D10_PWM/SS, J6.pin8, J2.pin3
  N10: Componente1.D11_PWM/MOSI, J6.pin7, J2.pin4
  N11: Componente1.D12/MISO, J6.pin6, J2.pin5
  N12: Componente1.D13/SCK, J6.pin5, J2.pin6
  N13: Componente1.GND, J6.pin4, RESET.4, R2.Pin_1, C1.1, C2.1, J2.pin7, J11.pin1, J11.pin2, J11.pin3, J11.pin4, J11.pin5, J4.pin6, J12.pin2, J12.pin3
  N14: Componente1.AREF, J6.pin3, J2.pin8
  N15: Componente1.D0/RX, J5.pin8, J1.pin1
  N16: Componente1.D1/TX, J5.pin7, J1.pin2
  N17: Componente1.D2, J5.pin6, J1.pin3
  N18: Componente1.D3_PWM, J5.pin5, J1.pin4
  N19: Componente1.D4, J5.pin4, J1.pin5
  N20: Componente1.D5_PWM, J5.pin3, J1.pin6
  N21: Componente1.D6_PWM, J5.pin2, J1.pin7
  N22: Componente1.D7, J5.pin1, J1.pin8
  N23: Componente1.ioref, J4.pin2, J12.pin7
  N24: Componente1.RESET, RESET.2, J4.pin3, J12.pin6
  N25: Componente1.3V3, J4.pin4, J12.pin5
  N26: Componente1.5V, R1.Pin_0, POWER.anode, C1.2, C2.2, J9.pin1, J9.pin2, J9.pin3, J9.pin4, J9.pin5, J4.pin5, J12.pin4
  N27: Componente1.VIN, J4.pin7, J12.pin1
  N28: Componente1.N/C, J4.pin1, J12.pin8
  N29: R1.Pin_1, RESET.1
  N30: POWER.cathode, R2.Pin_0

notes:
  GND
  5V
  IOREF
  RST
  3V3
  VIN
  A0
  A1
  A2
  A3
  A4
  A5
  AREF
  13
  12
  11
  ScrewShield
  1.0
  10
  9
  8
  7
  6
  5
  4
  3
  2
  1
  0
  https://github.com/nehenemilabs/ScrewShield
